# Fritzing sketch DeskLifter (saved by Fritzing 0.9.3b)
breadboards: 1

parts:
  Bauteil1 = SRF05 Ultrasonic Rangefinder
  Gizwits_WiFi_Witty_ESP-12F1 = Gizwits WiFi Witty ESP-12F
  S1 = SWITCH-MOMENTARY-2 [package=tactile_switch_smd-2]
  S2 = SWITCH-MOMENTARY-2 [package=tactile_switch_smd-2]
  R1 = Resistor [tolerance=±5% resistance=220 package="2010 [SMD]"]
  4_Channel_Relay1 = 4 Channel Power Relay
  R2 = Resistor [tolerance=±5% resistance=220 package="2010 [SMD]"]

nets:
  N1: Bauteil1.Trig, Gizwits_WiFi_Witty_ESP-12F1.GPIO2
  N2: Bauteil1.Echo, Gizwits_WiFi_Witty_ESP-12F1.GPIO0
  GND: Bauteil1.GND, Gizwits_WiFi_Witty_ESP-12F1.GND, R1.Pin_1, 4_Channel_Relay1.GND, R2.Pin_1
  N3: Gizwits_WiFi_Witty_ESP-12F1.GPIO12, 4_Channel_Relay1.IN2
  N4: Gizwits_WiFi_Witty_ESP-12F1.GPIO13, 4_Channel_Relay1.IN1
  VCC: Gizwits_WiFi_Witty_ESP-12F1.VCC, S1.2, S2.2, 4_Channel_Relay1.VCC
  N5: Gizwits_WiFi_Witty_ESP-12F1.GPIO4, S1.1, R1.Pin_0
  N6: Gizwits_WiFi_Witty_ESP-12F1.GPIO5, S2.1, R2.Pin_0

custom parts:
  4 Channel Power Relay: A 4 channel power relay. The module operates at 5V.
